# Fritzing sketch picar (saved by Fritzing 0.9.3b)

parts:
  Mod1 = Raspberry Pi 4B
  HC-SR04_Sensor_1 = HC-SR04 Ultrasonic Distance Sensor  # not connected
  Part1 = FC-03 [chip_label=FC-03]  # not connected
  Part2 = KY-033 Tracing Black White Line Hunting Sensor Module For Arduino  # not connected
  Mod2 = KY-010 Photo Interrupter Module [package="Breakout board"]  # not connected
  M1 = DC Motor  # not connected
  M2 = DC Motor  # not connected
  M3 = DC Motor  # not connected
  M4 = DC Motor  # not connected
  U1 = Molex Picoblade Series Header [part_number=0532610619 package=Picoblade-53261-0619]  # not connected
  U2 = Hirose DF13 Series Header [part_number=DF13#-5P-1.25V package=DF13C-5P-1.25V]  # not connected
  Pi_Cam_v2 = Rasberry Pi NIOR Camera [chip_label=IC package="DIP (Dual Inline) [THT]"]  # not connected
  Servo = Basic Servo  # not connected
  Part3 = RPi hat - blank [part_number=RPI-blank]

nets:
  3V3: Mod1.3V3, Mod1.GPIO4, Part3.3.3V, Part3.GPIO4
  N1: Mod1.5V, Part3.5.0V
  GND: Mod1.GPIO2, Mod1.GND, Mod1.GPIO14, Mod1.GPIO15, Mod1.GPIO17, Part3.GND, Part3.SDA, Part3.TXD, Part3.RXD, Part3.GPIO17
  N2: Mod1.GPIO3, Mod1.ID_SC, Part3.EECLK, Part3.SCL
  N3: Mod1.GPIO18, Mod1.ID_SD, Part3.EEDATA, Part3.GPIO18
  N4: Mod1.GPIO27, Mod1.GPIO26, Part3.GPIO26, Part3.GPIO27
  N5: Mod1.GPIO22, Part3.GPIO22
  N6: Mod1.GPIO23, Part3.GPIO23
  N7: Mod1.GPIO24, Part3.GPIO24
  N8: Mod1.GPIO10, Part3.SPI_MOSI
  N9: Mod1.GPIO9, Part3.SPI_MISO
  N10: Mod1.GPIO25, Part3.GPIO25
  N11: Mod1.GPIO11, Part3.SPI_SCLK
  N12: Mod1.GPIO8, Part3.SPI_CE0
  N13: Mod1.GPIO7, Part3.SPI_CE1
  N14: Mod1.GPIO5, Part3.GPIO5
  N15: Mod1.GPIO6, Part3.GPIO6
  N16: Mod1.GPIO12, Part3.GPIO12
  N17: Mod1.GPIO13, Part3.GPIO13
  N18: Mod1.GPIO19, Part3.GPIO19
  N19: Mod1.GPIO16, Part3.GPIO16
  N20: Mod1.GPIO20, Part3.GPIO20
  N21: Mod1.GPIO21, Part3.GPIO21

notes:
  Pi Camera Module
  Ultrasonic Sensor
  Motor 1
  Motor 2
  Motor 3
  Motor 4
  Photo-Interruptor

custom parts:
  FC-03: FC-03, LM393 IR Speed Sensor Encoder
  KY-033 Tracing Black White Line Hunting Sensor Module For Arduino: Tracing Black White Line Hunting Sensor Module For Arduino Description: This is KY-033 tracking sensor. The KY-033 measures the intensity of infrared radiation and delivers it as an analog output voltage. Features: Operating voltage: 2.5 - 12V(cannot over12V) working current: 18mA-20mA at 5V Enhanced accuracy Documents: http://www.vishay.com/docs/83760/tcrt5000.pdf
  KY-010 Photo Interrupter Module: KY-010 Photo Interrupter Module, it will trigger a signal when light between the sensor's gap is blocked.
  Rasberry Pi NIOR Camera: Camera
